# Fritzing sketch practica01 (saved by Fritzing 0.9.2b)
circuit board: 8.46667cm x 5.64444cm
breadboards: 1

parts:
  Practica01 = Arduino Uno (Rev3)
  POTENCIÓMETRO = Rotary Potentiometer (Small) [maximum_resistance=100kΩ package=THT]
  R2 = Resistor [tolerance=±5% resistance=220 package=THT]
  R3 = Resistor [tolerance=±5% resistance=220 package=THT]
  LED2 = LED - 5mm [color="Orange (620nm)" package="5 mm [THT]"]
  LED3 = LED - 5mm [color="Red (660nm)" package="5 mm [THT]"]
  R4 = Resistor [tolerance=±5% resistance=220 package=THT]
  LED1 = LED - 5mm [color="Green (560nm)" package="5 mm [THT]"]

nets:
  N1: Practica01.A0, POTENCIÓMETRO.wiper
  N2: Practica01.GND, POTENCIÓMETRO.leg2, LED2.cathode, LED3.cathode, LED1.cathode
  N3: Practica01.D3_PWM, R4.Pin_1
  N4: Practica01.D4, R2.Pin_1
  N5: Practica01.D5_PWM, R3.Pin_1
  N6: Practica01.5V, POTENCIÓMETRO.leg1
  N7: R2.Pin_0, LED2.anode
  N8: R3.Pin_0, LED3.anode
  N9: R4.Pin_0, LED1.anode
