# Fritzing sketch practica03 (saved by Fritzing 0.9.2b)
breadboards: 1

parts:
  R1 = Rotary Potentiometer (Large) [maximum_resistance=100kΩ package=THT]
  LED1 = green LED - 5mm
  LED2 = yellow LED - 5mm
  Parte1 = Arduino Uno (Rev3) - ICSP
  R2 = Resistor [tolerance=±5% resistance=220 package="1206 [SMD]"]
  R3 = Resistor [tolerance=±5% resistance=220 package="1206 [SMD]"]

nets:
  N1: R1.leg1, LED1.cathode, LED2.cathode, Parte1.GND
  N2: R1.wiper, Parte1.A0
  N3: R1.leg2, Parte1.5V
  N4: LED1.anode, R3.Pin_0
  N5: LED2.anode, R2.Pin_0
  N6: Parte1.D3_PWM, R3.Pin_1
  N7: Parte1.D4, R2.Pin_1
