# Fritzing sketch practica04 (saved by Fritzing 0.9.2b)
circuit board: 2.93648cm x 5.30154cm

parts:
  Parte1 = Arduino Uno (Rev3)
  o1 = Module display OLED I2C 128x64 SSD1306 [package=THT]

nets:
  N1: Parte1.A4/SDA, o1.SDA
  N2: Parte1.A5/SCL, o1.SCL
  5V: Parte1.5V, o1.VCC
  GND: Parte1.GND, o1.GND

notes:
  LCD I2C 20X4

custom parts:
  Module display OLED I2C 128x64 SSD1306: Ecran OLED I2C SSD163 de 128x64 avec connexion I2C
