# Fritzing sketch practica06 (saved by Fritzing 0.9.2b)
breadboards: 1

parts:
  R1 = Resistor [tolerance=±5% resistance=10k package=THT]
  S1 = Pushbutton [package="[THT]"]
  Parte1 = Arduino Uno (Rev3) - ICSP
  LCD1 = LCD 20x04

nets:
  N1: R1.Pin_0, S1.Pin_1, S1.Pin_2, Parte1.D2
  3V3: R1.Pin_1, Parte1.3V3, LCD1.VDD
  5V: S1.Pin_3, S1.Pin_4, Parte1.5V, LCD1.VSS
  N2: Parte1.A4/SDA, LCD1.RS
  N3: Parte1.A5/SCL, LCD1.V0

notes:
  I2C SETUP

custom parts:
  LCD 20x04: LCD 2004 character display, 4x rows of 20x characters. Blue.
